// Logisim project control.circ as structural Verilog: 1 circuit, main circuit cntrl
module cntrl (
  input  start,
  input  lsb,
  input  c32,
  input  CLK,
  input  Reset,
  output resOF,
  output init,
  output wadd,
  output wshift,
  output count
);

  wire and_6_out, and_7_out, and_8_out, and_9_out, and_10_out, and_11_out, and_12_out, and_13_out,
       and_14_out, and_15_out, not_1_out, not_2_out, not_3_out, not_4_out, not_5_out, not_6_out, not_7_out,
       not_8_out, not_9_out, not_10_out, not_11_out, not_12_out, not_13_out, not_14_out, not_15_out,
       not_16_out, not_17_out;
  wire [2:0] or_3_out, register_1_q;

  Register #(.width(3)) register_1 (.D(or_3_out), .en(1'b1), .Q(register_1_q), .clk(CLK), .clr(Reset));
  not not_1 (not_1_out, register_1_q[1]);
  not not_2 (not_2_out, register_1_q[2]);
  not not_3 (not_3_out, register_1_q[1]);
  and and_1 (wadd, register_1_q[1], register_1_q[0]);
  not not_4 (not_4_out, register_1_q[1]);
  not not_5 (not_5_out, register_1_q[0]);
  not not_6 (not_6_out, register_1_q[1]);
  not not_7 (not_7_out, register_1_q[0]);
  not not_8 (not_8_out, lsb);
  not not_9 (not_9_out, register_1_q[0]);
  not not_10 (not_10_out, register_1_q[1]);
  not not_11 (not_11_out, register_1_q[0]);
  not not_12 (not_12_out, register_1_q[1]);
  not not_13 (not_13_out, register_1_q[0]);
  not not_14 (not_14_out, register_1_q[2]);
  not not_15 (not_15_out, register_1_q[0]);
  not not_16 (not_16_out, register_1_q[1]);
  not not_17 (not_17_out, register_1_q[0]);
  and and_2 (resOF, register_1_q[2], not_1_out, register_1_q[0]);
  and and_3 (init, not_2_out, not_3_out, register_1_q[0]);
  and and_4 (wshift, register_1_q[2], not_4_out, not_5_out);
  and and_5 (count, register_1_q[2], not_6_out, not_7_out);
  and and_6 (and_6_out, register_1_q[1], not_8_out);
  and and_7 (and_7_out, register_1_q[1], register_1_q[0]);
  and and_8 (and_8_out, register_1_q[2], not_9_out);
  and and_9 (and_9_out, register_1_q[2], c32);
  and and_10 (and_10_out, not_10_out, register_1_q[0]);
  and and_11 (and_11_out, register_1_q[1], not_11_out, lsb);
  or or_1 (or_3_out[1], and_10_out, and_11_out, and_12_out);
  and and_12 (and_12_out, register_1_q[2], register_1_q[1]);
  and and_13 (and_13_out, not_12_out, not_13_out, start);
  and and_14 (and_14_out, not_14_out, register_1_q[1], not_15_out, lsb);
  and and_15 (and_15_out, register_1_q[2], not_16_out, not_17_out);
  or or_2 (or_3_out[2], and_6_out, and_7_out, and_8_out, and_9_out);
  or or_3 (or_3_out[0], and_13_out, and_14_out, and_15_out);
endmodule
