// Logisim project datapath.circ as structural Verilog: 5 circuits, main circuit Datapath
module Datapath (
  input  ResOF,
  input  [31:0] Multiplicand,
  input  [31:0] Multiplier,
  input  Init,
  input  WAdd,
  input  WShift,
  input  Cnt,
  input  CLK,
  output [31:0] msb,
  output PrdctLSB,
  output [31:0] lsb,
  output Count32
);

  wire Adder_cout, not_1_out, not_2_out, not_3_out, not_4_out, not_5_out, OF_Bit_q, or_1_out, or_2_out;
  wire [5:0] counter_1_q;
  wire [31:0] Adder_result, multiplexer_1_out, multiplexer_2_out, multiplexer_3_out, Multiplicand_q,
       shifter_1_lsb32o, shifter_1_msb32o;

  Counter #(.width(6), .max('h3f)) counter_1 (
    .count(Cnt), .Q(counter_1_q), .clk(CLK), .clr(Init));  // open: load, D, carry
  Register #(.width(32)) u_Multiplicand (.D(Multiplicand), .en(Init), .Q(Multiplicand_q), .clk(CLK));  // open: clr
  Multiplexer #(.width(32), .enable("false")) multiplexer_1 (
    .in0(Adder_result), .in1(shifter_1_msb32o), .out(multiplexer_1_out), .sel(WShift));
  or or_1 (or_1_out, Init, WShift);
  not not_1 (not_1_out, counter_1_q[0]);
  not not_2 (not_2_out, counter_1_q[1]);
  not not_3 (not_3_out, counter_1_q[2]);
  not not_4 (not_4_out, counter_1_q[3]);
  not not_5 (not_5_out, counter_1_q[4]);
  Adder Adder (.A(Multiplicand_q), .B(msb), .Cout(Adder_cout), .Result(Adder_result), .Cin(1'b0));
  Register #(.width(32)) ProductMSB32 (.D(multiplexer_2_out), .en(or_2_out), .Q(msb), .clk(CLK));  // open: clr
  Multiplexer #(.width(32), .enable("false")) multiplexer_2 (
    .in0(multiplexer_1_out), .in1({32{1'b0}}), .out(multiplexer_2_out), .sel(Init));
  or or_2 (or_2_out, WAdd, or_1_out);
  and and_1 (Count32, not_1_out, not_2_out, not_3_out, not_4_out, not_5_out, counter_1_q[5]);
  Multiplexer #(.width(32), .enable("false")) multiplexer_3 (
    .in0(shifter_1_lsb32o), .in1(Multiplier), .out(multiplexer_3_out), .sel(Init));
  Register #(.width(32)) ProductLSB32 (.D(multiplexer_3_out), .en(or_1_out), .Q(lsb), .clk(CLK));  // open: clr
  Register #(.width(1)) OF_Bit (.D(Adder_cout), .en(WAdd), .Q(OF_Bit_q), .clk(CLK), .clr(ResOF));
  Shifter shifter_1 (
    .Shift(WShift), .ShiftBit(OF_Bit_q), .MSB32(msb), .LSB32(lsb), .MSB32O(shifter_1_msb32o),
    .LSB32O(shifter_1_lsb32o));

  assign PrdctLSB = lsb[0];
endmodule

// Shift
module Shifter (
  input  Shift,
  input  ShiftBit,
  input  [31:0] MSB32,
  input  [31:0] LSB32,
  output [31:0] MSB32O,
  output [31:0] LSB32O
);

  Multiplexer #(.width(32), .enable("false")) multiplexer_1 (
    .in0(MSB32), .in1({ShiftBit, MSB32[31:1]}), .out(MSB32O), .sel(Shift));
  Multiplexer #(.width(32), .enable("false")) multiplexer_2 (
    .in0(LSB32), .in1({MSB32[0], LSB32[31:1]}), .out(LSB32O), .sel(Shift));
endmodule

module Adder (
  input  [31:0] A,
  input  [31:0] B,
  input  Cin,
  output Cout,
  output [31:0] Result
);

  wire n4_bit_adder_2_cout, n4_bit_adder_3_cout, n4_bit_adder_4_cout, n4_bit_adder_5_cout,
       n4_bit_adder_6_cout, n4_bit_adder_7_cout, n4_bit_adder_8_cout;

  _4_Bit_Adder u_4_bit_adder_1 (
    .A(A[31:28]), .B(B[31:28]), .Cout(Cout), .Cin(n4_bit_adder_2_cout), .Result(Result[31:28]));
  _4_Bit_Adder u_4_bit_adder_2 (
    .A(A[27:24]), .B(B[27:24]), .Cout(n4_bit_adder_2_cout), .Cin(n4_bit_adder_3_cout), .Result(Result[27:24]));
  _4_Bit_Adder u_4_bit_adder_3 (
    .A(A[23:20]), .B(B[23:20]), .Cout(n4_bit_adder_3_cout), .Cin(n4_bit_adder_4_cout), .Result(Result[23:20]));
  _4_Bit_Adder u_4_bit_adder_4 (
    .A(A[19:16]), .B(B[19:16]), .Cout(n4_bit_adder_4_cout), .Cin(n4_bit_adder_5_cout), .Result(Result[19:16]));
  _4_Bit_Adder u_4_bit_adder_5 (
    .A(A[15:12]), .B(B[15:12]), .Cout(n4_bit_adder_5_cout), .Cin(n4_bit_adder_6_cout), .Result(Result[15:12]));
  _4_Bit_Adder u_4_bit_adder_6 (
    .A(A[11:8]), .B(B[11:8]), .Cout(n4_bit_adder_6_cout), .Cin(n4_bit_adder_7_cout), .Result(Result[11:8]));
  _4_Bit_Adder u_4_bit_adder_7 (
    .A(A[7:4]), .B(B[7:4]), .Cout(n4_bit_adder_7_cout), .Cin(n4_bit_adder_8_cout), .Result(Result[7:4]));
  _4_Bit_Adder u_4_bit_adder_8 (.A(A[3:0]), .B(B[3:0]), .Cout(n4_bit_adder_8_cout), .Cin(Cin), .Result(Result[3:0]));
endmodule

module _1_Bit_Full_Adder (
  input  A,
  input  B,
  input  Cin,
  output Result,
  output Cout
);

  wire and_1_out, and_2_out, xor_1_out;

  xor xor_1 (xor_1_out, A, B);
  xor xor_2 (Result, xor_1_out, Cin);
  and and_1 (and_1_out, Cin, xor_1_out);
  and and_2 (and_2_out, B, A);
  or or_1 (Cout, and_1_out, and_2_out);
endmodule

module _4_Bit_Adder (
  input  [3:0] A,
  input  [3:0] B,
  input  Cin,
  output Cout,
  output [3:0] Result
);

  wire n1_bit_full_adder_2_cout, n1_bit_full_adder_3_cout, n1_bit_full_adder_4_cout;

  _1_Bit_Full_Adder u_1_bit_full_adder_1 (
    .A(A[3]), .B(B[3]), .Cin(n1_bit_full_adder_2_cout), .Result(Result[3]), .Cout(Cout));
  _1_Bit_Full_Adder u_1_bit_full_adder_2 (
    .A(A[2]), .B(B[2]), .Cin(n1_bit_full_adder_3_cout), .Result(Result[2]), .Cout(n1_bit_full_adder_2_cout));
  _1_Bit_Full_Adder u_1_bit_full_adder_3 (
    .A(A[1]), .B(B[1]), .Cin(n1_bit_full_adder_4_cout), .Result(Result[1]), .Cout(n1_bit_full_adder_3_cout));
  _1_Bit_Full_Adder u_1_bit_full_adder_4 (
    .A(A[0]), .B(B[0]), .Cin(Cin), .Result(Result[0]), .Cout(n1_bit_full_adder_4_cout));
endmodule
