// Logisim project mult32.circ as structural Verilog: 1 circuit, main circuit main
module main (
  input  Start,
  input  Reset,
  output [31:0] MostS_32,
  output [31:0] LeastS_32
);

  wire clock_1_out, cntrl_1_count, cntrl_1_init, cntrl_1_resof, cntrl_1_wadd, cntrl_1_wshift,
       datapath_1_count32, datapath_1_prdctlsb;

  Clock clock_1 (.out(clock_1_out));
  Datapath datapath_1 (
    .ResOF(cntrl_1_resof), .Multiplicand({32{1'b1}}), .Multiplier(32'h2), .Init(cntrl_1_init),
    .WAdd(cntrl_1_wadd), .WShift(cntrl_1_wshift), .Cnt(cntrl_1_count), .CLK(clock_1_out), .msb(MostS_32),
    .PrdctLSB(datapath_1_prdctlsb), .lsb(LeastS_32), .Count32(datapath_1_count32));
  cntrl cntrl_1 (
    .start(Start), .lsb(datapath_1_prdctlsb), .c32(datapath_1_count32), .CLK(clock_1_out), .Reset(Reset),
    .resOF(cntrl_1_resof), .init(cntrl_1_init), .wadd(cntrl_1_wadd), .wshift(cntrl_1_wshift),
    .count(cntrl_1_count));

  // Notes on the sheet:
  //   Multiplicand
  //   Multiplier
  //   RESULT
endmodule
